// Logisim project parte1_cache.circ as structural Verilog: 1 circuit, main circuit main
module main (
  input  [5:0] Endereco,
  input  [15:0] entradaDados,
  input  in_3,
  input  Clock,
  input  in_5,
  input  in_6,
  input  Resetar,
  output ACERTO,
  output [7:0] DADO_LIDO,
  output FALTA
);

  wire decoder_1_out0, decoder_1_out1, decoder_1_out2, decoder_1_out3, L0_ANDmiss_out, l0_q, L1_AND_MISS_out,
       l1_q, L2_AND_MISS_out, l2_q, L3_AND_MISS_out, l3_q, multiplexer_1_out, not_1_out, or_5_out, xor_1_out,
       xor_2_out, xor_3_out;
  wire [3:0] counter_1_q, or_1_out;
  wire [15:0] Dados_dout;

  D_Flip_Flop l0 (.D(or_1_out[0]), .clk(Clock), .Q(l0_q), .reset(Resetar));  // open: Qn, preset
  D_Flip_Flop l1 (.D(or_1_out[1]), .clk(Clock), .Q(l1_q), .reset(Resetar));  // open: Qn, preset
  D_Flip_Flop l2 (.D(or_1_out[2]), .clk(Clock), .Q(l2_q), .reset(Resetar));  // open: Qn, preset
  D_Flip_Flop l3 (.D(or_1_out[3]), .clk(Clock), .Q(l3_q), .reset(Resetar));  // open: Qn, preset
  or or_1 (or_1_out[0], l0_q, L0_ANDmiss_out);
  or or_2 (or_1_out[1], l1_q, L1_AND_MISS_out);
  or or_3 (or_1_out[2], l2_q, L2_AND_MISS_out);
  or or_4 (or_1_out[3], l3_q, L3_AND_MISS_out);
  Decoder #(.select(2)) decoder_1 (
    .out0(decoder_1_out0), .out1(decoder_1_out1), .out2(decoder_1_out2), .out3(decoder_1_out3),
    .sel(Endereco[2:1]));  // open: en
  Multiplexer #(.select(2)) multiplexer_1 (
    .in0(l0_q), .in1(l1_q), .in2(l2_q), .in3(l3_q), .out(multiplexer_1_out), .sel(Endereco[2:1]));
  and L0_ANDmiss (L0_ANDmiss_out, decoder_1_out0, FALTA);
  and L1_AND_MISS (L1_AND_MISS_out, decoder_1_out1, FALTA);
  RAM #(.addrWidth(2), .dataWidth(3)) TAG (
    .addr(Endereco[2:1]), .we(FALTA), .oe(1'b1), .clk(Clock), .din(Endereco[5:3]), .dout({in_3, in_5, in_6}));
  RAM #(.addrWidth(2), .dataWidth(16)) Dados (
    .addr(Endereco[2:1]), .we(FALTA), .oe(1'b1), .clk(Clock), .din(entradaDados), .dout(Dados_dout));
  and L2_AND_MISS (L2_AND_MISS_out, decoder_1_out2, FALTA);
  and L3_AND_MISS (L3_AND_MISS_out, decoder_1_out3, FALTA);
  Multiplexer #(.width(8)) multiplexer_2 (
    .in0(Dados_dout[7:0]), .in1(Dados_dout[15:8]), .out(DADO_LIDO), .sel(Endereco[0]));
  xor xor_1 (xor_1_out, Endereco[3], in_6);
  xor xor_2 (xor_2_out, Endereco[4], in_5);
  xor xor_3 (xor_3_out, Endereco[5], in_3);
  or or_5 (or_5_out, xor_1_out, xor_2_out, xor_3_out);
  not not_1 (not_1_out, or_5_out);
  and and_1 (ACERTO, not_1_out, multiplexer_1_out);
  not not_2 (FALTA, ACERTO);
  Counter #(.max('hf), .width(4)) counter_1 (
    .clr(Resetar), .count(ACERTO), .clk(Clock), .Q(counter_1_q));  // open: load, up, D, carry
  Hex_Digit_Display hex_digit_display_1 (.value(counter_1_q));  // open: dp

  // Notes on the sheet:
  //   bits validos 0 - 3
  //   0 - offset
  //   2-1 indice 
  //   5-3 tag
  //   ATIVA BIT VALIDO SEM SOBRESCREVER ESTADO ANTERIOR
  //   TAG enderecamento
  //   T0 - T2
  //   TAG da linha acessada
  //   S0 - S2
  //   2 bytes
  //   offset seleciona um dos 2 bytes de dados
  //   iguais
  //   iguais . valido[indice]
  //   MISS
  //   HIT
endmodule
