// Logisim project maquinaDeEstadosUC.circ as structural Verilog: 1 circuit, main circuit main
module main (
  input  OP,
  input  Reset
);

  wire and_1_out, and_2_out, and_3_out, and_4_out, and_5_out, clock_1_out, d_ff_1_qn, d_ff_2_q, d_ff_2_qn,
       d_ff_3_q, d_ff_3_qn, not_1_out, or_1_out;

  Clock clock_1 (.out(clock_1_out));
  not not_1 (not_1_out, OP);
  D_Flip_Flop d_ff_1 (.D(and_2_out), .clk(clock_1_out), .Qn(d_ff_1_qn), .reset(Reset));  // open: Q, preset
  D_Flip_Flop d_ff_2 (.D(or_1_out), .clk(clock_1_out), .Q(d_ff_2_q), .Qn(d_ff_2_qn), .reset(Reset));  // open: preset
  D_Flip_Flop d_ff_3 (.D(and_1_out), .clk(clock_1_out), .Q(d_ff_3_q), .Qn(d_ff_3_qn), .reset(Reset));  // open: preset
  and and_1 (and_1_out, d_ff_1_qn, d_ff_3_qn);
  and and_2 (and_2_out, not_1_out, and_5_out);
  and and_3 (and_3_out, d_ff_2_q, d_ff_3_qn);
  and and_4 (and_4_out, OP, and_5_out);
  and and_5 (and_5_out, d_ff_1_qn, d_ff_2_qn, d_ff_3_q);
  or or_1 (or_1_out, and_3_out, and_4_out);

  // Notes on the sheet:
  //   Q2
  //   Q1
  //   Q0
  //   LogicaD2
  //   LogicaD0
  //   logicaD1
  //   Sinal de estado S1
  //   a máquina está em S1(001)
endmodule
